// Logisim project EP2.circ as structural Verilog: 4 circuits, main circuit testULA
module testULA (
  input  [7:0] in_1,
  input  [7:0] in_2,
  input  in_3,
  output [7:0] out_4
);

  wire ula_1_c0, ula_1_c1, ula_1_c2, ula_1_c3, ula_1_c4, ula_1_c5, ula_1_o1, ula_1_o2;

  ULA ula_1 (
    .A(in_1), .B(in_2), .OP(in_3), .R(out_4), .o1(ula_1_o1), .o2(ula_1_o2), .c0(ula_1_c0), .c1(ula_1_c1),
    .c2(ula_1_c2), .c3(ula_1_c3), .c4(ula_1_c4), .c5(ula_1_c5));
  LED SignedOverflow (.in(ula_1_o1));
  LED UnsignedOverflow (.in(ula_1_o2));
  LED AmoreB_unsigned (.in(ula_1_c0));
  LED AlessB_unsigned (.in(ula_1_c1));
  LED AequalB (.in(ula_1_c2));
  LED Aequal0 (.in(ula_1_c3));
  LED AmoreB_signed (.in(ula_1_c4));
  LED AlessB_signed (.in(ula_1_c5));
endmodule

module ULA (
  input  [7:0] A,
  input  [7:0] B,
  input  OP,
  output [7:0] R,
  output o1,
  output o2,
  output c0,
  output c1,
  output c2,
  output c3,
  output c4,
  output c5
);

  full_adder_8bit full_adder_8bit_1 (.A(A), .B(B), .OP(OP), .R(R), .SignedOverflow(o1), .UnsignedOverflow(o2));
  comparator_8bit comparator_8bit_1 (.A(A), .B(B), .S(1'b0), .AmorethenB(c0), .AequalB(c2), .AlessthenB(c1));
  comparator_8bit comparator_8bit_2 (.A(A), .B({8{1'b0}}), .AequalB(c3));  // open: S, AmorethenB, AlessthenB
  comparator_8bit comparator_8bit_3 (.A(A), .B(B), .S(1'b1), .AmorethenB(c4), .AlessthenB(c5));  // open: AequalB
endmodule

module comparator_8bit (
  input  S,
  input  [7:0] A,
  input  [7:0] B,
  output AmorethenB,
  output AequalB,
  output AlessthenB
);

  wire a7, b7, comparator_1bit_1_aequaltob, comparator_1bit_1_alessthenb, comparator_1bit_1_amorethenb,
       comparator_1bit_2_aequaltob, comparator_1bit_2_alessthenb, comparator_1bit_2_amorethenb,
       comparator_1bit_3_aequaltob, comparator_1bit_3_alessthenb, comparator_1bit_3_amorethenb,
       comparator_1bit_4_aequaltob, comparator_1bit_4_alessthenb, comparator_1bit_4_amorethenb,
       comparator_1bit_5_aequaltob, comparator_1bit_5_alessthenb, comparator_1bit_5_amorethenb,
       comparator_1bit_6_aequaltob, comparator_1bit_6_alessthenb, comparator_1bit_6_amorethenb,
       comparator_1bit_7_aequaltob, comparator_1bit_7_alessthenb, comparator_1bit_7_amorethenb;

  comparator_1bit comparator_1bit_1 (
    .A(a7), .B(b7), .AequalB_input(1'b1), .AmorethenB(comparator_1bit_1_amorethenb),
    .AequaltoB(comparator_1bit_1_aequaltob), .AlessthenB(comparator_1bit_1_alessthenb));  // open: AlessB_input, AmoreB_input
  xor xor_1 (a7, A[7], S);
  xor xor_2 (b7, B[7], S);
  comparator_1bit comparator_1bit_2 (
    .A(A[6]), .B(B[6]), .AlessB_input(comparator_1bit_1_alessthenb),
    .AequalB_input(comparator_1bit_1_aequaltob), .AmoreB_input(comparator_1bit_1_amorethenb),
    .AmorethenB(comparator_1bit_2_amorethenb), .AequaltoB(comparator_1bit_2_aequaltob),
    .AlessthenB(comparator_1bit_2_alessthenb));
  comparator_1bit comparator_1bit_3 (
    .A(A[5]), .B(B[5]), .AlessB_input(comparator_1bit_2_alessthenb),
    .AequalB_input(comparator_1bit_2_aequaltob), .AmoreB_input(comparator_1bit_2_amorethenb),
    .AmorethenB(comparator_1bit_3_amorethenb), .AequaltoB(comparator_1bit_3_aequaltob),
    .AlessthenB(comparator_1bit_3_alessthenb));
  comparator_1bit comparator_1bit_4 (
    .A(A[4]), .B(B[4]), .AlessB_input(comparator_1bit_3_alessthenb),
    .AequalB_input(comparator_1bit_3_aequaltob), .AmoreB_input(comparator_1bit_3_amorethenb),
    .AmorethenB(comparator_1bit_4_amorethenb), .AequaltoB(comparator_1bit_4_aequaltob),
    .AlessthenB(comparator_1bit_4_alessthenb));
  comparator_1bit comparator_1bit_5 (
    .A(A[3]), .B(B[3]), .AlessB_input(comparator_1bit_4_alessthenb),
    .AequalB_input(comparator_1bit_4_aequaltob), .AmoreB_input(comparator_1bit_4_amorethenb),
    .AmorethenB(comparator_1bit_5_amorethenb), .AequaltoB(comparator_1bit_5_aequaltob),
    .AlessthenB(comparator_1bit_5_alessthenb));
  comparator_1bit comparator_1bit_6 (
    .A(A[2]), .B(B[2]), .AlessB_input(comparator_1bit_5_alessthenb),
    .AequalB_input(comparator_1bit_5_aequaltob), .AmoreB_input(comparator_1bit_5_amorethenb),
    .AmorethenB(comparator_1bit_6_amorethenb), .AequaltoB(comparator_1bit_6_aequaltob),
    .AlessthenB(comparator_1bit_6_alessthenb));
  comparator_1bit comparator_1bit_7 (
    .A(A[1]), .B(B[1]), .AlessB_input(comparator_1bit_6_alessthenb),
    .AequalB_input(comparator_1bit_6_aequaltob), .AmoreB_input(comparator_1bit_6_amorethenb),
    .AmorethenB(comparator_1bit_7_amorethenb), .AequaltoB(comparator_1bit_7_aequaltob),
    .AlessthenB(comparator_1bit_7_alessthenb));
  comparator_1bit comparator_1bit_8 (
    .A(A[0]), .B(B[0]), .AlessB_input(comparator_1bit_7_alessthenb),
    .AequalB_input(comparator_1bit_7_aequaltob), .AmoreB_input(comparator_1bit_7_amorethenb),
    .AmorethenB(AmorethenB), .AequaltoB(AequalB), .AlessthenB(AlessthenB));
endmodule

module comparator_1bit (
  input  A,
  input  B,
  input  AlessB_input,
  input  AequalB_input,
  input  AmoreB_input,
  output AmorethenB,
  output AequaltoB,
  output AlessthenB
);

  wire and_1_out, and_2_out, and_3_out, and_5_out, not_1_out, xor_1_out, xor_2_out;

  xor xor_1 (xor_1_out, A, B);
  not not_1 (not_1_out, xor_1_out);
  xor xor_2 (xor_2_out, A, B);
  and and_1 (and_1_out, A, xor_2_out);
  and and_2 (and_2_out, xor_2_out, B);
  and and_3 (and_3_out, and_1_out, AequalB_input);
  and and_4 (AequaltoB, not_1_out, AequalB_input);
  and and_5 (and_5_out, and_2_out, AequalB_input);
  or or_1 (AlessthenB, AlessB_input, and_5_out);
  or or_2 (AmorethenB, and_3_out, AmoreB_input);
endmodule
