// Logisim project EP1.circ as structural Verilog: 6 circuits, main circuit testADDER
module full_adder_8bit (
  input  [7:0] A,
  input  [7:0] B,
  input  OP,
  output [7:0] R,
  output SignedOverflow,
  output UnsignedOverflow
);

  wire adder_8bit_1_c7, controlled_inverter_8bit_1_out0, controlled_inverter_8bit_1_out1,
       controlled_inverter_8bit_1_out2, controlled_inverter_8bit_1_out3, controlled_inverter_8bit_1_out4,
       controlled_inverter_8bit_1_out5, controlled_inverter_8bit_1_out6, controlled_inverter_8bit_1_out7;

  controlled_inverter_8bit controlled_inverter_8bit_1 (
    .in0(B[0]), .in1(B[1]), .in2(B[2]), .in3(B[3]), .in4(B[4]), .in5(B[5]), .in6(B[6]), .in7(B[7]),
    .inverterSignal(OP), .out0(controlled_inverter_8bit_1_out0), .out1(controlled_inverter_8bit_1_out1),
    .out2(controlled_inverter_8bit_1_out2), .out3(controlled_inverter_8bit_1_out3),
    .out4(controlled_inverter_8bit_1_out4), .out5(controlled_inverter_8bit_1_out5),
    .out6(controlled_inverter_8bit_1_out6), .out7(controlled_inverter_8bit_1_out7));
  adder_8bit adder_8bit_1 (
    .a3(A[3]), .b3(controlled_inverter_8bit_1_out3), .a0(A[0]), .b0(controlled_inverter_8bit_1_out0),
    .c0(OP), .a4(A[4]), .b4(controlled_inverter_8bit_1_out4), .a5(A[5]),
    .b5(controlled_inverter_8bit_1_out5), .a6(A[6]), .b6(controlled_inverter_8bit_1_out6), .a7(A[7]),
    .b7(controlled_inverter_8bit_1_out7), .a1(A[1]), .b1(controlled_inverter_8bit_1_out1), .a2(A[2]),
    .b2(controlled_inverter_8bit_1_out2), .s2(R[2]), .s3(R[3]), .s4(R[4]), .s5(R[5]), .s6(R[6]),
    .c7(adder_8bit_1_c7), .s7(R[7]), .c8(UnsignedOverflow), .s0(R[0]), .s1(R[1]));
  xor xor_1 (SignedOverflow, adder_8bit_1_c7, UnsignedOverflow);
endmodule

module adder_1bit (
  input  inA,
  input  inB,
  input  inCarry,
  output outSum,
  output outCarry
);

  wire and_1_out, and_2_out, xor_1_out;

  xor xor_1 (xor_1_out, inA, inB);
  and and_1 (and_1_out, xor_1_out, inCarry);
  and and_2 (and_2_out, inA, inB);
  xor xor_2 (outSum, inCarry, xor_1_out);
  or or_1 (outCarry, and_1_out, and_2_out);
endmodule

module adder_8bit (
  input  a0,
  input  a1,
  input  a2,
  input  a3,
  input  a4,
  input  a5,
  input  a6,
  input  a7,
  input  b0,
  input  b1,
  input  b2,
  input  b3,
  input  b4,
  input  b5,
  input  b6,
  input  b7,
  input  c0,
  output s0,
  output s1,
  output s2,
  output s3,
  output s4,
  output s5,
  output s6,
  output c7,
  output s7,
  output c8
);

  wire adder_1bit_1_outcarry, adder_1bit_2_outcarry, adder_1bit_3_outcarry, adder_1bit_4_outcarry,
       adder_1bit_5_outcarry, adder_1bit_6_outcarry;

  adder_1bit adder_1bit_1 (.inA(a0), .inB(b0), .inCarry(c0), .outSum(s0), .outCarry(adder_1bit_1_outcarry));
  adder_1bit adder_1bit_2 (
    .inA(a1), .inB(b1), .inCarry(adder_1bit_1_outcarry), .outSum(s1), .outCarry(adder_1bit_2_outcarry));
  adder_1bit adder_1bit_3 (
    .inA(a2), .inB(b2), .inCarry(adder_1bit_2_outcarry), .outSum(s2), .outCarry(adder_1bit_3_outcarry));
  adder_1bit adder_1bit_4 (
    .inA(a3), .inB(b3), .inCarry(adder_1bit_3_outcarry), .outSum(s3), .outCarry(adder_1bit_4_outcarry));
  adder_1bit adder_1bit_5 (
    .inA(a4), .inB(b4), .inCarry(adder_1bit_4_outcarry), .outSum(s4), .outCarry(adder_1bit_5_outcarry));
  adder_1bit adder_1bit_6 (
    .inA(a5), .inB(b5), .inCarry(adder_1bit_5_outcarry), .outSum(s5), .outCarry(adder_1bit_6_outcarry));
  adder_1bit adder_1bit_7 (.inA(a6), .inB(b6), .inCarry(adder_1bit_6_outcarry), .outSum(s6), .outCarry(c7));
  adder_1bit adder_1bit_8 (.inA(a7), .inB(b7), .inCarry(c7), .outSum(s7), .outCarry(c8));
endmodule

module controlled_inverter_8bit (
  input  in0,
  input  in1,
  input  in2,
  input  in3,
  input  in4,
  input  in5,
  input  in6,
  input  in7,
  input  inverterSignal,
  output out0,
  output out1,
  output out2,
  output out3,
  output out4,
  output out5,
  output out6,
  output out7
);

  controlled_inverter_1bit controlled_inverter_1bit_1 (
    .inverterIn(in0), .inverterSignal(inverterSignal), .inverterOut(out0));
  controlled_inverter_1bit controlled_inverter_1bit_2 (
    .inverterIn(in1), .inverterSignal(inverterSignal), .inverterOut(out1));
  controlled_inverter_1bit controlled_inverter_1bit_3 (
    .inverterIn(in2), .inverterSignal(inverterSignal), .inverterOut(out2));
  controlled_inverter_1bit controlled_inverter_1bit_4 (
    .inverterIn(in3), .inverterSignal(inverterSignal), .inverterOut(out3));
  controlled_inverter_1bit controlled_inverter_1bit_5 (
    .inverterIn(in4), .inverterSignal(inverterSignal), .inverterOut(out4));
  controlled_inverter_1bit controlled_inverter_1bit_6 (
    .inverterIn(in5), .inverterSignal(inverterSignal), .inverterOut(out5));
  controlled_inverter_1bit controlled_inverter_1bit_7 (
    .inverterIn(in6), .inverterSignal(inverterSignal), .inverterOut(out6));
  controlled_inverter_1bit controlled_inverter_1bit_8 (
    .inverterIn(in7), .inverterSignal(inverterSignal), .inverterOut(out7));
endmodule

module controlled_inverter_1bit (
  input  inverterIn,
  input  inverterSignal,
  output inverterOut
);

  xor xor_1 (inverterOut, inverterIn, inverterSignal);
endmodule

module testADDER (
  input  [7:0] in_1,
  input  [7:0] in_2,
  input  in_3,
  output [7:0] out_4
);

  wire full_adder_8bit_1_signedoverflow, full_adder_8bit_1_unsignedoverflow;

  full_adder_8bit full_adder_8bit_1 (
    .A(in_1), .B(in_2), .OP(in_3), .R(out_4), .SignedOverflow(full_adder_8bit_1_signedoverflow),
    .UnsignedOverflow(full_adder_8bit_1_unsignedoverflow));
  LED SignedOverflow (.in(full_adder_8bit_1_signedoverflow));
  LED UnsignedOverflow (.in(full_adder_8bit_1_unsignedoverflow));
endmodule
