// Logisim project EP3.circ as structural Verilog: 3 circuits, main circuit main
module main (
  input  [7:0] STDIN,
  output [7:0] STDOUT,
  output Overflow
);

  wire AE, CLK, DMX2, MUX1, MUX2, MUX3, MUX4, OP, PE, PJ, RI, RO;
  wire [1:0] DMX1;
  wire [2:0] Comps;
  wire [7:0] demultiplexer_1_out0, demultiplexer_1_out1, demultiplexer_2_out3, multiplexer_2_out,
       multiplexer_3_out, multiplexer_4_out, pc_1_pcout, register_1_q, register_1_q_2, register_2_q,
       transistor_1_out, ula_1_r;
  wire [15:0] demultiplexer_2_out0, demultiplexer_2_out1, demultiplexer_2_out2, multiplexer_1_out, ram_1_dout;

  Clock clock_1 (.out(CLK));
  Register #(.width(16)) register_1 (
    .D(demultiplexer_2_out0), .en(1'b1), .Q({register_1_q_2, register_1_q}), .clk(CLK), .clr(PE));
  UC uc_1 (
    .Less(Comps[0]), .Greater(Comps[2]), .Equal(Comps[1]), .in_1(register_1_q_2), .MUX4(MUX4), .DMX1(DMX1),
    .DMX2(DMX2), .RamIn(RI), .RamOut(RO), .OP(OP), .accEn(AE), .PCJump(PJ), .PCEnd(PE), .MUX1(MUX1),
    .MUX2(MUX2), .MUX3(MUX3));  // open: RST
  // Probe on DMX1
  Transistor #(.\type ("n"), .width(8)) transistor_1 (.in(register_1_q), .out(transistor_1_out), .gate(PJ));
  PC pc_1 (.CLK(CLK), .JMP(PJ), .JMP_ADDR(transistor_1_out), .PCOut(pc_1_pcout));
  Multiplexer #(.width(16)) multiplexer_1 (
    .in0(demultiplexer_2_out2), .in1({16{1'b0}}), .out(multiplexer_1_out), .sel(MUX3));
  Multiplexer #(.width(8)) multiplexer_2 (.in0(STDIN), .in1(demultiplexer_1_out0), .out(multiplexer_2_out), .sel(MUX4));
  Multiplexer #(.width(8)) multiplexer_3 (
    .in0(demultiplexer_2_out1[7:0]), .in1(ula_1_r), .out(multiplexer_3_out), .sel(MUX2));
  Demultiplexer #(.width(8)) demultiplexer_1 (
    .out0(demultiplexer_1_out0), .out1(demultiplexer_1_out1), .in(register_2_q), .sel(DMX2));
  Multiplexer #(.width(8)) multiplexer_4 (.in0(pc_1_pcout), .in1(register_1_q), .out(multiplexer_4_out), .sel(MUX1));
  Register register_2 (.D(multiplexer_3_out), .en(AE), .Q(register_2_q), .clk(CLK), .clr(PE));
  RAM #(.clearpin("true"), .dataWidth(16), .enables("line")) ram_1 (
    .addr(multiplexer_4_out), .we(RI), .clk(CLK), .din({{8{1'b0}}, multiplexer_2_out}), .dout(ram_1_dout),
    .clr(PE));
  ULA ula_1 (
    .A(demultiplexer_1_out1), .B(multiplexer_1_out[7:0]), .OP(OP), .R(ula_1_r), .o1(Overflow), .c2(Comps[1]),
    .c4(Comps[2]), .c5(Comps[0]));  // open: o2, c0, c1, c3
  Demultiplexer #(.select(2), .tristate("true"), .width(16)) demultiplexer_2 (
    .out0(demultiplexer_2_out0), .out1(demultiplexer_2_out1), .out2(demultiplexer_2_out2),
    .out3({demultiplexer_2_out3, STDOUT}), .in(ram_1_dout), .sel(DMX1));
  // also tied to GND on the sheet: {demultiplexer_2_out3[0], demultiplexer_2_out3[1], demultiplexer_2_out3[2], demultiplexer_2_out3[3], demultiplexer_2_out3[4], demultiplexer_2_out3[5], demultiplexer_2_out3[6], demultiplexer_2_out3[7]}

  // Notes on the sheet:
  //   NUSP: 11260186
  //   Leonardo Heidi Almeida Murakami
  //   AequalB
  //   AgreaterB 
  //   AlessB
endmodule

module UC (
  input  [7:0] in_1,
  input  RST,
  input  Less,
  input  Greater,
  input  Equal,
  output MUX1,
  output MUX2,
  output MUX3,
  output MUX4,
  output [1:0] DMX1,
  output DMX2,
  output RamIn,
  output RamOut,
  output OP,
  output accEn,
  output PCJump,
  output PCEnd
);

  wire and_1_out, and_2_out, and_3_out, and_4_out, and_5_out, and_6_out, and_7_out, and_8_out, and_9_out,
       and_10_out, and_11_out, and_12_out, and_13_out, and_14_out, and_15_out, j_k_ff_1_q, nand_1_out,
       not_1_out, not_2_out, or_1_out;
  wire [2:0] multiplexer_1_out;

  not not_1 (not_1_out, RST);
  not not_2 (not_2_out, not_1_out);
  and and_1 (and_1_out, not_2_out, not_1_out);
  or or_1 (or_1_out, or_1_out, and_1_out);
  nand nand_1 (nand_1_out, or_1_out, RST);
  J_K_Flip_Flop j_k_ff_1 (.J(1'b1), .K(nand_1_out), .clk(1'b1), .Q(j_k_ff_1_q));  // open: Qn, preset, reset
  and and_2 (and_2_out, PCEnd, j_k_ff_1_q);
  Multiplexer #(.width(4)) multiplexer_1 (
    .in0(in_1[3:0]), .in1(4'b0000), .out({MUX3, multiplexer_1_out}), .sel(and_2_out));
  and and_3 (and_3_out, ~MUX3, multiplexer_1_out[2]);  // AND_Gate
  and and_4 (and_4_out, ~MUX3, ~multiplexer_1_out[2], multiplexer_1_out[0]);  // AND_Gate
  and and_5 (and_5_out, ~MUX3, multiplexer_1_out[1]);  // AND_Gate
  and and_6 (and_6_out, MUX3, ~multiplexer_1_out[1], ~multiplexer_1_out[0]);  // AND_Gate
  or or_2 (MUX1, and_3_out, and_4_out, and_5_out, and_6_out);
  or or_3 (MUX2, multiplexer_1_out[2], multiplexer_1_out[1]);
  not not_3 (MUX4, multiplexer_1_out[0]);
  and and_7 (and_7_out, ~multiplexer_1_out[1], multiplexer_1_out[0]);  // AND_Gate
  or or_4 (DMX1[0], and_7_out, MUX3);
  or or_5 (DMX1[1], MUX3, multiplexer_1_out[2], multiplexer_1_out[1]);
  or or_6 (DMX2, ~multiplexer_1_out[1], multiplexer_1_out[0]);  // OR_Gate
  and and_8 (and_8_out, ~MUX3, multiplexer_1_out[2], multiplexer_1_out[1], multiplexer_1_out[0]);  // AND_Gate
  or or_7 (RamIn, and_8_out, and_9_out);
  and and_9 (and_9_out, ~MUX3, ~multiplexer_1_out[2], multiplexer_1_out[1], ~multiplexer_1_out[0]);  // AND_Gate
  and and_10 (and_10_out, ~multiplexer_1_out[2], multiplexer_1_out[0]);  // AND_Gate
  or or_8 (RamOut, ~multiplexer_1_out[1], and_10_out);  // OR_Gate
  not not_4 (OP, multiplexer_1_out[0]);
  and and_11 (and_11_out, ~MUX3, multiplexer_1_out[2], ~multiplexer_1_out[1], ~multiplexer_1_out[0]);  // AND_Gate
  and and_12 (and_12_out, ~MUX3, ~multiplexer_1_out[2], multiplexer_1_out[0]);  // AND_Gate
  or or_9 (accEn, and_11_out, and_12_out);
  and and_13 (and_13_out, MUX3, ~multiplexer_1_out[2], multiplexer_1_out[1], ~multiplexer_1_out[0]);  // AND_Gate
  and and_14 (and_14_out, Greater, MUX3, ~multiplexer_1_out[2], multiplexer_1_out[1], multiplexer_1_out[0]);  // AND_Gate
  and and_15 (and_15_out, Equal, MUX3, multiplexer_1_out[2], ~multiplexer_1_out[1], multiplexer_1_out[0]);  // AND_Gate
  or or_10 (PCJump, and_13_out, and_14_out, and_15_out);
  and and_16 (PCEnd, MUX3, ~multiplexer_1_out[2], ~multiplexer_1_out[1], multiplexer_1_out[0]);  // AND_Gate

  // Other names for the same wires on the sheet: DMX1_0 = DMX1[0]; DMX1_1 = DMX1[1]
endmodule

module PC (
  input  CLK,
  input  JMP,
  input  [7:0] JMP_ADDR,
  output [7:0] PCOut
);

  wire and_1_out, and_2_out, and_3_out, and_4_out, and_5_out, and_6_out, and_7_out, and_8_out, and_9_out,
       and_10_out, and_11_out, and_12_out, and_13_out, and_14_out, and_15_out, and_16_out, and_17_out,
       and_18_out, and_19_out, and_20_out, and_21_out, and_22_out, j_k_ff_1_q;

  J_K_Flip_Flop j_k_ff_1 (.J(1'b1), .K(1'b1), .clk(CLK), .Q(j_k_ff_1_q));  // open: Qn, preset, reset
  J_K_Flip_Flop j_k_ff_2 (
    .J(1'b1), .clk(j_k_ff_1_q), .K(1'b1), .Q(PCOut[0]), .preset(and_1_out), .reset(and_2_out));  // open: Qn
  and and_1 (and_1_out, JMP, JMP_ADDR[0]);
  and and_2 (and_2_out, JMP, ~JMP_ADDR[0]);  // AND_Gate
  and and_3 (and_3_out, JMP, JMP_ADDR[1]);
  J_K_Flip_Flop j_k_ff_3 (
    .J(PCOut[0]), .clk(j_k_ff_1_q), .K(PCOut[0]), .Q(PCOut[1]), .preset(and_3_out), .reset(and_4_out));  // open: Qn
  and and_4 (and_4_out, JMP, ~JMP_ADDR[1]);  // AND_Gate
  and and_5 (and_5_out, PCOut[0], PCOut[1]);
  and and_6 (and_6_out, JMP, JMP_ADDR[2]);
  J_K_Flip_Flop j_k_ff_4 (
    .J(and_5_out), .clk(j_k_ff_1_q), .K(and_5_out), .Q(PCOut[2]), .preset(and_6_out), .reset(and_7_out));  // open: Qn
  and and_7 (and_7_out, JMP, ~JMP_ADDR[2]);  // AND_Gate
  and and_8 (and_8_out, and_5_out, PCOut[2]);
  J_K_Flip_Flop j_k_ff_5 (
    .J(and_8_out), .clk(j_k_ff_1_q), .K(and_8_out), .Q(PCOut[3]), .preset(and_9_out), .reset(and_10_out));  // open: Qn
  and and_9 (and_9_out, JMP, JMP_ADDR[3]);
  and and_10 (and_10_out, JMP, ~JMP_ADDR[3]);  // AND_Gate
  and and_11 (and_11_out, and_8_out, PCOut[3]);
  J_K_Flip_Flop j_k_ff_6 (
    .J(and_11_out), .clk(j_k_ff_1_q), .K(and_11_out), .Q(PCOut[4]), .preset(and_12_out), .reset(and_13_out));  // open: Qn
  and and_12 (and_12_out, JMP, JMP_ADDR[4]);
  and and_13 (and_13_out, JMP, ~JMP_ADDR[4]);  // AND_Gate
  and and_14 (and_14_out, and_11_out, PCOut[4]);
  J_K_Flip_Flop j_k_ff_7 (
    .J(and_14_out), .clk(j_k_ff_1_q), .K(and_14_out), .Q(PCOut[5]), .preset(and_15_out), .reset(and_16_out));  // open: Qn
  and and_15 (and_15_out, JMP, JMP_ADDR[5]);
  and and_16 (and_16_out, JMP, ~JMP_ADDR[5]);  // AND_Gate
  and and_17 (and_17_out, and_14_out, PCOut[5]);
  J_K_Flip_Flop j_k_ff_8 (
    .J(and_17_out), .K(and_17_out), .Q(PCOut[6]), .preset(and_18_out), .reset(and_19_out));  // open: clk, Qn
  and and_18 (and_18_out, JMP, JMP_ADDR[6]);
  and and_19 (and_19_out, JMP, ~JMP_ADDR[6]);  // AND_Gate
  and and_20 (and_20_out, and_17_out, PCOut[6]);
  J_K_Flip_Flop j_k_ff_9 (
    .J(and_20_out), .clk(j_k_ff_1_q), .K(and_20_out), .Q(PCOut[7]), .preset(and_21_out), .reset(and_22_out));  // open: Qn
  and and_21 (and_21_out, JMP, JMP_ADDR[7]);
  and and_22 (and_22_out, JMP, ~JMP_ADDR[7]);  // AND_Gate
endmodule
